# Fritzing sketch Milestone2 (saved by Fritzing 0.9.3b)
breadboards: 1

parts:
  Part1 = Arduino Uno (Rev3)
  IC1 = L293D [package=THT]
  VCC1 = 4 x AAA Battery Mount
  VCC2 = 4 x AAA Battery Mount
  S1 = Pushbutton [package="[THT]"]
  S2 = SPST Switch [package=switch-spdt_lock.007s]
  J1 = Piezo Speaker
  R1 = Resistor [tolerance=±5% resistance=220 package="2512 [SMD]"]
  M1 = DC Motor
  M2 = DC Motor

nets:
  N1: Part1.D11_PWM/MOSI, S1.Pin_1, S1.Pin_2, R1.Pin_1
  N2: Part1.D12/MISO, J1.pin2
  N3: Part1.D3_PWM, IC1.In_1
  N4: Part1.D4, IC1.In_2
  N5: Part1.D6_PWM, IC1.In_4
  N6: Part1.D7, IC1.In_3
  N7: IC1.Enable_1, IC1.Enable_2, IC1.+V, VCC2.+, S2.P, R1.Pin_0
  N8: IC1.Out_1_(_Controlled_by_Enable_1_), M2.pin_1
  N9: IC1.0V, VCC1.-, VCC2.-, S1.Pin_3, S1.Pin_4, S2.O, J1.pin1
  N10: IC1.Out_2_(_Controlled_by_Enable_1_), M2.pin_2
  N11: IC1.+Vmotor, VCC1.+
  N12: IC1.Out_3_(_Controlled_by_Enable_2_), M1.pin_2
  N13: IC1.Out_4_(_Controlled_by_Enable_2_), M1.pin_1

notes:
  Left Motor
  Right Motor
  220 ohm
